# Fritzing sketch Lauflicht (saved by Fritzing 0.7.12b)
breadboards: 1

parts:
  LED1 = LED - 5mm [color="Red (633nm)" package="5 mm [THT]"]
  R1 = Resistor [tolerance=±5% resistance=220 package=THT]
  LED2 = LED - 5mm [color="Red (633nm)" package="5 mm [THT]"]
  LED3 = LED - 5mm [color="Red (633nm)" package="5 mm [THT]"]
  LED4 = LED - 5mm [color="Red (633nm)" package="5 mm [THT]"]
  LED5 = LED - 5mm [color="Red (633nm)" package="5 mm [THT]"]
  LED6 = LED - 5mm [color="Red (633nm)" package="5 mm [THT]"]
  R2 = Resistor [tolerance=±5% resistance=220 package=THT]
  R3 = Resistor [tolerance=±5% resistance=220 package=THT]
  R4 = Resistor [tolerance=±5% resistance=220 package=THT]
  R5 = Resistor [tolerance=±5% resistance=220 package=THT]
  R6 = Resistor [tolerance=±5% resistance=220 package=THT]
  Arduino1 = Arduino

nets:
  N1: LED1.cathode, LED2.cathode, LED3.cathode, LED4.cathode, LED5.cathode, LED6.cathode, Arduino1.GND
  N2: LED1.anode, R1.Pin_0
  N3: R1.Pin_1, Arduino1.D7
  N4: LED2.anode, R2.Pin_0
  N5: LED3.anode, R3.Pin_0
  N6: LED4.anode, R4.Pin_0
  N7: LED5.anode, R5.Pin_0
  N8: LED6.anode, R6.Pin_0
  N9: R2.Pin_1, Arduino1.D6
  N10: R3.Pin_1, Arduino1.D5
  N11: R4.Pin_1, Arduino1.D4
  N12: R5.Pin_1, Arduino1.D3
  N13: R6.Pin_1, Arduino1.D2

// code stored in the sketch: Lauflicht.bas
int ledPin[] = {2,3,4,5,6,7}; //ledPin0=2, ledPin1=3, ... 
int ledPin13 = 13;
boolean led13 = false;

// the setup routine runs once when you press reset:
void setup() {     
  pinMode(ledPin13, OUTPUT); 
  
  for(int i=0;i<=5;i++){
    pinMode(ledPin[i], OUTPUT);  
  } 
 
}

// the loop routine runs over and over again forever:
void loop() {
  lauflos();
}

void lauflos() {
  
  if(led13==true){
    digitalWrite(ledPin13, LOW);
    led13=false;
  }
  else{
    digitalWrite(led13, HIGH);
    led13=true;
  }
  
  for(int i=0;i<=5;i++){
    digitalWrite(ledPin[i], HIGH);
    delay(200);   
    digitalWrite(ledPin[i], LOW);
  }
  for(int i=4;i>=1;i--){
    digitalWrite(ledPin[i], HIGH);
    delay(200);   
    digitalWrite(ledPin[i], LOW);
  }
}
