# Fritzing sketch Taster (saved by Fritzing 0.7.12b)
breadboards: 1

parts:
  Arduino1 = Arduino
  R1 = Resistor [tolerance=±5% resistance=220 package=THT]
  LED1 = LED - 5mm [color="Red (633nm)" package="5 mm [THT]"]
  S1 = Pushbutton [package="[THT]"]

nets:
  N1: Arduino1.D13, LED1.anode
  N2: Arduino1.D8, S1.Pin_3, S1.Pin_4
  N3: R1.Pin_0, LED1.cathode
  N4: R1.Pin_1, S1.Pin_1, S1.Pin_2
