# Fritzing sketch WWLuefter_Fritzing (saved by Fritzing 0.7.12b)
breadboards: 1

parts:
  Nano1 = Arduino Nano v2.3
  R1 = 330 Ω Resistor [package=THT]
  R2 = 330 Ω Resistor [package=THT]
  R3 = 330 Ω Resistor [package=THT]
  R4 = 330 Ω Resistor [package=THT]
  R5 = 330 Ω Resistor [package=THT]
  LED1 = green LED - 5mm
  LED2 = green LED - 5mm
  LED3 = yellow LED - 5mm
  LED4 = yellow LED - 5mm
  LED5 = Red LED - 5mm [package="5 mm [THT]"]
  Q1 = NPN-Transistor [package="TO92 [THT]"]
  D1 = Rectifier Diode [part_number=1N4001 package="300 mil [THT]"]
  T1 = LM35 Temperature Sensor [package="TO92 [THT]"]
  T2 = LM35 Temperature Sensor [package="TO92 [THT]"]
  R6 = 330k Ω Resistor [package=THT]
  Q2 = NPN-Transistor [package="TO92 [THT]"]
  M1 = DC Motor
  M2 = DC Motor
  D2 = Rectifier Diode [part_number=1N4001 package="300 mil [THT]"]

nets:
  GND: Nano1.GND, LED1.cathode, LED2.cathode, LED3.cathode, LED4.cathode, LED5.cathode, Q1.E, T1.+Vs, T1.GND, T2.+Vs, T2.GND, Q2.E
  N1: Nano1.D4, T1.Vout, T2.Vout, R6.Pin_1
  N2: Nano1.D5, R5.Pin_0
  N3: Nano1.D6, R4.Pin_0
  N4: Nano1.D7, R3.Pin_0
  N5: Nano1.D8, R2.Pin_0
  N6: Nano1.D9, R1.Pin_0
  N7: Nano1.D11, Q1.B
  N8: Nano1.D12, Q2.B
  N9: Nano1.VIN, D1.cathode, R6.Pin_0, M1.pin_1, M2.pin_1, D2.cathode
  N10: R1.Pin_1, LED1.anode
  N11: R2.Pin_1, LED2.anode
  N12: R3.Pin_1, LED3.anode
  N13: R4.Pin_1, LED4.anode
  N14: R5.Pin_1, LED5.anode
  N15: Q1.C, D1.anode, M1.pin_2
  N16: Q2.C, M2.pin_2, D2.anode
